// Logisim project RISC 32 BIT MAIN.circ as structural Verilog: 1 circuit, main circuit main
module main (
  input  [31:0] in_1
);

  wire Arithmetic, Clock, CLR, EnOP1, EnRC, HALT, LD, Logic, MOV;
  wire [2:0] Instr, OPCODE;
  wire [7:0] Dest;
  wire [15:0] Input;
  wire [31:0] multiplexer_1_out, OP1, OP2, Result;

  Clock clock_1 (.out(Clock));
  RISC_32_BIT_ALU_main main_1 (
    .Clock(Clock), .Result(Result), .OP1(OP1), .OP2(OP2), .OpeartionCode(OPCODE), .in_1(Instr));
  RISC_32_BIT_DECODE_main main_2 (
    .Clock(Clock), .out_34(LD), .out_36(MOV), .out_37(CLR), .out_38(HALT), .out_39(Dest),
    .out_40(Input[15:8]), .out_41(Input[7:0]), .Instruction(in_1), .Arithmetic(Arithmetic), .Logic(Logic),
    .out_5(Instr), .out_6(OPCODE));  // open: out_3, out_4, out_7, out_8, out_9, out_10, out_11, out_12, out_13, out_14, out_15, out_16, out_17, out_18, out_19, out_20, out_21, out_22, out_23, out_24, out_25, out_26, out_32, out_33, out_35, out_42, BranchJump, RegInstr, Stack
  Multiplexer #(.width(32)) multiplexer_1 (
    .in0({{16{1'b0}}, Input}), .in1(OP1), .out(multiplexer_1_out), .sel(EnOP1), .en(1'b1));
  buf or_1 (EnOP1, MOV);  // OR_Gate
  or or_2 (EnRC, Arithmetic, Logic, MOV, LD);
  RISC_32_BIT_REGISTERS_main main_3 (
    .in_4(Dest[4:0]), .in_5(Dest[4:0]), .in_6(Input[12:8]), .in_7(Input[4:0]), .in_8(Clock), .out_13(OP1),
    .out_14(OP2), .in_3(multiplexer_1_out), .in_9(EnRC), .in_10(CLR), .in_11(EnOP1));  // open: in_12, in_2, in_1

  // Other names for the same wires on the sheet: RC[4:0] = Dest[4:0]; O2[7:0] = Input[7:0]; REG2[4:0] = Input[4:0];
  //   O1[7:0] = Input[15:8]; REG1[4:0] = Input[12:8]
endmodule
